# Fritzing sketch Cryo Interface Board (saved by Fritzing 0.9.3b)
circuit board: 10cm x 5cm
breadboards: 1

parts:
  Ardweeny = atmega328 [package=dip]
  Thermocouple = female pin header, 6 pins [form="♀ (female)" part_number="G V+CKSO -CS"]
  J1 = female pin header, 8 pins [form="♀ (female)" part_number="V - CK- DC -CS"]  # not connected
  OLED = female pin header, 8 pins [form="♀ (female)" part_number="G - SD- DO -RST"]
  DB9 = female pin header, 4 pins [form="♀ (female)" part_number="RXTX G V"]
  -Power+ = female pin header, 2 pins [form="♀ (female)"]
  Switch = SPST Switch [package=switch-spdt]
  10k = Resistor [tolerance=±5% resistance=10k package=THT]
  Trimpot = TRIMPOT [package=trimpot_pth_s3_lock]
  Coarse_Opto = IC, DIP package, 4 pins [chip_label=IC]
  Fine_opto = IC, DIP package, 4 pins [chip_label=IC]
  Trimpot_2 = TRIMPOT [package=trimpot_pth_s3_lock]
  470 = Resistor [tolerance=±5% resistance=220 package=THT]
  3_3V_reg = V_REG_LD1117VXX [package=78xxl]
  470_2 = Resistor [tolerance=±5% resistance=220 package=THT]
  RC = Resistor [tolerance=±5% resistance=220 package=THT]
  RF = Resistor [tolerance=±5% resistance=220 package=THT]
  C+ = Ceramic Capacitor [capacitance=100nF package="100 mil [THT, multilayer]"]
  -Cryo+ = female pin header, 2 pins [form="♀ (female)"]
  Trimpot_3 = TRIMPOT [package=trimpot_pth_s3_lock]
  R-I = Resistor [tolerance=±5% resistance=10k package=THT]

nets:
  N1: Ardweeny.D2, DB9.pin1
  N2: Ardweeny.D3_(PWM), DB9.pin2
  N3: Ardweeny.D4, Switch.O, 10k.Pin_0
  N4: Ardweeny.VCC, Thermocouple.pin5, OLED.pin7, DB9.pin4, Switch.P, 3_3V_reg.OUT
  N5: Ardweeny.GND, Thermocouple.pin6, OLED.pin8, DB9.pin3, -Power+.pin2, 10k.Pin_1, Coarse_Opto.pin2, Fine_opto.pin2, 3_3V_reg.IN
  N6: Ardweeny.D5_(PWM), 470.Pin_0
  N7: Ardweeny.D6_(PWM), 470_2.Pin_0
  N8: Ardweeny.D7, Thermocouple.pin1
  N9: Ardweeny.D8, OLED.pin3
  N10: Ardweeny.D9_(PWM), OLED.pin2
  N11: Ardweeny.D10_(PWM), OLED.pin1
  N12: Ardweeny.D11_(PWM), OLED.pin6
  N13: Ardweeny.D12, Thermocouple.pin3
  N14: Ardweeny.D13, Thermocouple.pin4, OLED.pin5
  N15: -Power+.pin1, 3_3V_reg.GND
  N16: Trimpot.WIPER, RC.Pin_0
  N17: Trimpot.CW, Trimpot_2.CW, C+.1, -Cryo+.pin2, Trimpot_3.CW
  N18: Coarse_Opto.pin1, 470.Pin_1
  N19: Coarse_Opto.pin3, Fine_opto.pin3, C+.0, -Cryo+.pin1, R-I.Pin_0
  N20: Coarse_Opto.pin4, RC.Pin_1
  N21: Fine_opto.pin1, 470_2.Pin_1
  N22: Fine_opto.pin4, RF.Pin_0
  N23: Trimpot_2.WIPER, RF.Pin_1
  N24: Trimpot_3.WIPER, R-I.Pin_1
